# Fritzing sketch color-cycle (saved by Fritzing 0.7.1b)
breadboards: 1

parts:
  IC1 = TI MSP430(G2) Microcontroller [part_number=MSP430 package="DIP (Dual Inline) [THT]"]
  VCC1 = Battery
  R1 = Resistor [tolerance=±5% resistance=10k package=THT]
  LED3 = Super Flux RGB LED (com. anode)

nets:
  N1: IC1.VCC, VCC1.+, R1.Pin_1, LED3.common_anode
  N2: IC1.P1.0, LED3.green_cathode
  N3: IC1.P1.1, LED3.red_cathode
  N4: IC1.P1.2, LED3.blue_cathode
  N5: IC1.RST, R1.Pin_0
  N6: IC1.GND, VCC1.-

custom parts:
  TI MSP430(G2) Microcontroller: Texas Instruments MSP430G2x01/MSP430G2x11 Microcontroller. http://www.ti.com/lit/ds/slas695g/slas695g.pdf
